# Fritzing sketch ESP32LidarWiring (saved by Fritzing 0.9.8b)

parts:
  M1 = esp32_p30_w11 [part_number=ESP32S-PIN30]
  Lidar_Sensor = Adafruit VL530X Time of Flight Distance Sensor [part_number="Adafruit #3317"]

nets:
  N1: M1.connector0, Lidar_Sensor.VCC
  N2: M1.connector1, Lidar_Sensor.GND
  N3: M1.connector10, Lidar_Sensor.SDA
  N4: M1.connector13, Lidar_Sensor.SCL

custom parts:
  Adafruit VL530X Time of Flight Distance Sensor: The VL53L0X is a Time of Flight distance sensor like no other you've used! The sensor contains a very tiny invisible laser source, and a matching sensor. The VL53L0X can detect the "time of flight", or how long the light has taken to bounce back to the sensor. Since it uses a very narrow light source, it is good for determining distance of only the surface directly in front of it. Unlike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

// code stored in the sketch: LidarReadings.ino
#include "Adafruit_VL53L0X.h"

Adafruit_VL53L0X lox = Adafruit_VL53L0X();

void setup() {
  Serial.begin(115200);

  // wait until serial port opens for native USB devices
  while (! Serial) {
    delay(1);
  }
  
  Serial.println("Adafruit VL53L0X test");
  if (!lox.begin()) {
    Serial.println(F("Failed to boot VL53L0X"));
    while(1);
  }
  // power 
  Serial.println(F("VL53L0X API Simple Ranging example\n\n")); 
}


void loop() {
  VL53L0X_RangingMeasurementData_t measure;
    
  Serial.print("Reading a measurement... ");
  lox.rangingTest(&measure, false); // pass in 'true' to get debug data printout!

  if (measure.RangeStatus != 4) {  // phase failures have incorrect data
    Serial.print("Distance (mm): "); Serial.println(measure.RangeMilliMeter);
  } else {
    Serial.println(" out of range ");
  }
    
  delay(100);
}
