# Fritzing sketch RPI0ADCWiring (saved by Fritzing 0.9.8b)

parts:
  Part1 = Adafruit ADS1115 16Bit I2C ADC [part_number="Adafruit #1085"]
  MCU1 = Raspberry Pi Zero

nets:
  N1: Part1.SDA, MCU1.pin_3
  N2: Part1.SCL, MCU1.pin_5
  N3: Part1.GND, MCU1.pin_6, MCU1.pin_20
  N4: Part1.VDD, MCU1.pin_1

custom parts:
  Adafruit ADS1115 16Bit I2C ADC: For microcontrollers without an analog-to-digital converter or when you want a higher-precision ADC, the ADS1115 provides 16-bit precision at 860 samples/second over I2C. The chip can be configured as 4 single-ended input channels, or two differential channels. As a nice bonus, it even includes a programmable gain amplifier, up to x16, to help boost up smaller single/differential signals to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
