# Fritzing sketch RPI0UltrasonicWiring (saved by Fritzing 0.9.8b)
breadboards: 1

parts:
  MCU1 = Raspberry Pi Zero
  HC-SR04_Sensor_1 = HC-SR04 Ultrasonic Distance Sensor
  R3 = Resistor [tolerance=±1% power=0.25 resistance=2k package=THT]
  R2 = Resistor [tolerance=±1% power=0.25 resistance=1k package=THT]

nets:
  N1: MCU1.pin_4, HC-SR04_Sensor_1.VCC
  N2: MCU1.pin_6, MCU1.pin_34, MCU1.pin_39, HC-SR04_Sensor_1.GND, R3.Pin_1
  N3: MCU1.pin_12, HC-SR04_Sensor_1.TRIG
  N4: MCU1.pin_18, R3.Pin_0, R2.Pin_1
  N5: HC-SR04_Sensor_1.ECHO, R2.Pin_0
