# Fritzing sketch RPI0LidarWiring (saved by Fritzing 0.9.8b)
breadboards: 1

parts:
  MCU1 = Raspberry Pi Zero
  Part1 = Adafruit VL530X Time of Flight Distance Sensor [part_number="Adafruit #3317"]

nets:
  N1: MCU1.pin_1, Part1.VCC
  N2: MCU1.pin_3, Part1.SDA
  N3: MCU1.pin_5, Part1.SCL
  N4: MCU1.pin_9, Part1.GND

custom parts:
  Adafruit VL530X Time of Flight Distance Sensor: The VL53L0X is a Time of Flight distance sensor like no other you've used! The sensor contains a very tiny invisible laser source, and a matching sensor. The VL53L0X can detect the "time of flight", or how long the light has taken to bounce back to the sensor. Since it uses a very narrow light source, it is good for determining distance of only the surface directly in front of it. Unlike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
